# Fritzing sketch Switches (saved by Fritzing 0.9.2b)
circuit board: 9.17579cm x 7.70841cm
breadboards: 1

parts:
  U1 = Optocoupler [package=THT]
  U2 = Optocoupler [package=THT]
  U3 = Optocoupler [package=THT]
  U4 = Optocoupler [package=THT]
  U5 = Optocoupler [package=THT]
  U6 = Optocoupler [package=THT]
  R1 = Resistor [tolerance=±5% resistance=100 package="1206 [SMD]"]
  PWR = Screw terminal - 2 pins [package=THT]
  A1 = Screw terminal - 2 pins [package=THT]
  R2 = Resistor [tolerance=±5% resistance=100 package="1206 [SMD]"]
  S1 = Screw terminal - 2 pins [package=THT]
  S2 = Screw terminal - 2 pins [package=THT]
  A2 = Screw terminal - 2 pins [package=THT]
  S3 = Screw terminal - 2 pins [package=THT]
  S4 = Screw terminal - 2 pins [package=THT]
  S5 = Screw terminal - 2 pins [package=THT]
  S6 = Screw terminal - 2 pins [package=THT]
  A3 = Screw terminal - 2 pins [package=THT]
  R5 = Resistor [tolerance=±5% resistance=100 package="1206 [SMD]"]
  R6 = Resistor [tolerance=±5% resistance=100 package="1206 [SMD]"]
  R4 = Resistor [tolerance=±5% resistance=100 package="1206 [SMD]"]
  R3 = Resistor [tolerance=±5% resistance=100 package="1206 [SMD]"]
  A4 = Screw terminal - 2 pins [package=THT]
  A5 = Screw terminal - 2 pins [package=THT]
  A6 = Screw terminal - 2 pins [package=THT]

nets:
  N1: U1.Pin_1, R1.Pin_1
  N2: U1.Pin_2, S1.pin1
  N3: U1.Pin_4, A1.pin2
  N4: U1.Pin_5, A1.pin1
  N5: U2.Pin_1, R2.Pin_1
  N6: U2.Pin_2, S2.pin1
  N7: U2.Pin_4, A2.pin2
  N8: U2.Pin_5, A2.pin1
  N9: U3.Pin_1, R3.Pin_1
  N10: U3.Pin_2, S3.pin1
  N11: U3.Pin_4, A3.pin2
  N12: U3.Pin_5, A3.pin1
  N13: U4.Pin_1, R4.Pin_1
  N14: U4.Pin_2, S4.pin1
  N15: U4.Pin_4, A4.pin2
  N16: U4.Pin_5, A4.pin1
  N17: U5.Pin_1, R5.Pin_1
  N18: U5.Pin_2, S5.pin1
  N19: U5.Pin_4, A5.pin2
  N20: U5.Pin_5, A5.pin1
  N21: U6.Pin_1, R6.Pin_1
  N22: U6.Pin_2, S6.pin1
  N23: U6.Pin_4, A6.pin2
  N24: U6.Pin_5, A6.pin1
  N25: R1.Pin_0, PWR.pin2, R2.Pin_0, R5.Pin_0, R6.Pin_0, R4.Pin_0, R3.Pin_0
  N26: PWR.pin1, S1.pin2, S2.pin2, S3.pin2, S4.pin2, S5.pin2, S6.pin2
